# Fritzing sketch BusPivot-v1 (saved by Fritzing 0.9.3b)

parts:
  Part1 = Arduino Uno (Rev3)
  Part2 = InvenSense MPU6050
  J1 = Basic Servo
  JACK1 = 2.1mm Barrel Jack with Terminal Block

nets:
  N1: Part1.A4/SDA, Part2.SDA
  N2: Part1.A5/SCL, Part2.SCL
  N3: Part1.D9_PWM, J1.pulse
  5V: Part1.5V, Part2.VCC
  GND: Part1.GND, Part2.GND, J1.gnd, JACK1.NEG
  VIN: Part1.VIN, J1.vcc, JACK1.POS

notes:
  Door Servo
  5V
