# Fritzing sketch BusPivot-v2-1 (saved by Fritzing 0.9.3b)

parts:
  Part1 = Arduino Uno (Rev3)
  J1 = Basic Servo
  JACK1 = 2.1mm Barrel Jack with Terminal Block
  S1 = Round Pushbutton
  J2 = Basic Servo

nets:
  N1: Part1.D9_PWM, J1.pulse
  N2: Part1.D3_PWM, S1.leg0
  N3: Part1.D7, J2.pulse
  GND: Part1.GND, J1.gnd, JACK1.NEG, S1.leg1, J2.gnd
  VCC: Part1.VIN, J1.vcc, JACK1.POS, J2.vcc

notes:
  Door Servo
  5V
  Push Servo
